// Logisim project P17.circ as structural Verilog: 1 circuit, main circuit main
module main (
  input  in_1
);

  wire and_1_out, clock_1_out, d_ff_1_q, t_ff_1_q, t_ff_2_q;

  Clock clock_1 (.out(clock_1_out));
  LED led_1 ();  // open: in
  D_Flip_Flop d_ff_1 (.clk(clock_1_out), .D(in_1), .Q(d_ff_1_q));  // open: Qn, preset, en, reset
  LED led_2 ();  // open: in
  T_Flip_Flop t_ff_1 (.clk(clock_1_out), .T(d_ff_1_q), .Q(t_ff_1_q));  // open: Qn, preset, reset, en
  and and_1 (and_1_out, d_ff_1_q, t_ff_1_q);
  T_Flip_Flop t_ff_2 (.clk(clock_1_out), .T(and_1_out), .Q(t_ff_2_q));  // open: Qn, preset, reset, en
  LED led_3 ();  // open: in
endmodule
