// Logisim project P18.circ as structural Verilog: 1 circuit, main circuit main
module main (
  input  in_1,
  input  in_2,
  input  in_3
);

  wire and_1_out, and_2_out, and_3_out, and_4_out, not_1_out, or_1_out, or_2_out, t_ff_1_q, t_ff_1_qn,
       t_ff_2_q, t_ff_2_qn;

  not not_1 (not_1_out, in_1);
  T_Flip_Flop t_ff_1 (.clk(in_3), .T(in_2), .Q(t_ff_1_q), .Qn(t_ff_1_qn));  // open: preset, reset, en
  and and_1 (and_1_out, not_1_out, t_ff_1_q);
  and and_2 (and_2_out, in_1, t_ff_1_qn);
  buf or_1 (or_1_out, and_1_out);  // OR_Gate
  T_Flip_Flop t_ff_2 (.clk(in_3), .T(or_1_out), .Q(t_ff_2_q), .Qn(t_ff_2_qn));  // open: preset, reset, en
  and and_3 (and_3_out, and_1_out, t_ff_2_q);
  and and_4 (and_4_out, t_ff_2_qn, and_2_out);
  or or_2 (or_2_out, and_3_out, and_4_out);
  D_Flip_Flop d_ff_1 (.clk(in_3), .D(or_2_out));  // open: Q, Qn, preset, en, reset
endmodule
