// Logisim project P5.circ as structural Verilog
module F_a_b_c (
  input  a,
  input  b,
  input  c,
  output f
);

  wire and_1_out, not_1_out;

  not not_1 (not_1_out, a);
  and and_1 (and_1_out, not_1_out, b);
  or or_1 (f, c, and_1_out);
endmodule

module f_a_b_c (
  input  a,
  input  b,
  input  c,
  output f
);

  wire and_1_out, not_1_out;

  not not_1 (not_1_out, a);
  and and_1 (and_1_out, not_1_out, b);
  or or_1 (f, c, and_1_out);
endmodule

module f_abc (
  input  a,
  input  b,
  input  c,
  output f
);

  wire and_1_out, not_1_out;

  not not_1 (not_1_out, a);
  and and_1 (and_1_out, not_1_out, b);
  or or_1 (f, c, and_1_out);
endmodule

module F_A_B_C (
  input  A,
  input  B,
  input  C,
  output F
);

  wire and_1_out, not_1_out;

  not not_1 (not_1_out, A);
  and and_1 (and_1_out, not_1_out, B);
  or or_1 (F, C, and_1_out);
endmodule
